// Logisim project conway.circ as structural Verilog: 25 circuits, main circuit main_shift_based_v2
module popcount (
  input  A,
  input  B,
  input  C,
  input  D,
  input  E,
  input  F,
  input  G,
  input  H,
  output [3:0] CNT
);

  wire [3:0] adder_1_out, adder_2_out, adder_3_out, adder_4_out, adder_5_out, adder_6_out,
       bit_extender_1_out, bit_extender_2_out, bit_extender_3_out, bit_extender_4_out, bit_extender_5_out,
       bit_extender_6_out, bit_extender_7_out, bit_extender_8_out;

  assign bit_extender_1_out = {{3{1'b0}}, A};  // Bit_Extender bit_extender_1
  assign bit_extender_2_out = {{3{1'b0}}, B};  // Bit_Extender bit_extender_2
  assign bit_extender_3_out = {{3{1'b0}}, C};  // Bit_Extender bit_extender_3
  assign bit_extender_4_out = {{3{1'b0}}, D};  // Bit_Extender bit_extender_4
  assign bit_extender_5_out = {{3{1'b0}}, E};  // Bit_Extender bit_extender_5
  assign bit_extender_6_out = {{3{1'b0}}, F};  // Bit_Extender bit_extender_6
  assign bit_extender_7_out = {{3{1'b0}}, G};  // Bit_Extender bit_extender_7
  assign bit_extender_8_out = {{3{1'b0}}, H};  // Bit_Extender bit_extender_8
  Adder #(.width(4)) adder_1 (.a(bit_extender_1_out), .b(bit_extender_2_out), .out(adder_1_out));  // open: cin, cout
  Adder #(.width(4)) adder_2 (.a(bit_extender_3_out), .b(bit_extender_4_out), .out(adder_2_out));  // open: cin, cout
  Adder #(.width(4)) adder_3 (.a(bit_extender_5_out), .b(bit_extender_6_out), .out(adder_3_out));  // open: cin, cout
  Adder #(.width(4)) adder_4 (.a(bit_extender_7_out), .b(bit_extender_8_out), .out(adder_4_out));  // open: cin, cout
  Adder #(.width(4)) adder_5 (.a(adder_1_out), .b(adder_2_out), .out(adder_5_out));  // open: cin, cout
  Adder #(.width(4)) adder_6 (.a(adder_3_out), .b(adder_4_out), .out(adder_6_out));  // open: cin, cout
  Adder #(.width(4)) adder_7 (.a(adder_5_out), .b(adder_6_out), .out(CNT));  // open: cin, cout
endmodule

module full_adder (
  input  A,
  input  B,
  input  C_IN,
  output SUM,
  output CARRY
);

  wire and_1_out, and_2_out, and_3_out, xor_1_out;

  xor xor_1 (xor_1_out, A, B);
  and and_1 (and_1_out, A, B);
  and and_2 (and_2_out, A, C_IN);
  and and_3 (and_3_out, B, C_IN);
  xor xor_2 (SUM, xor_1_out, C_IN);
  or or_1 (CARRY, and_1_out, and_2_out, and_3_out);
endmodule

module popcount_manual (
  input  A,
  input  B,
  input  C,
  input  D,
  input  E,
  input  F,
  input  G,
  input  H,
  output [3:0] CNT
);

  wire [1:0] add1_sum, add2_sum, add3_sum, add4_sum;
  wire [2:0] add5_sum, add6_sum;

  full_adder_1_bit_to_2_bit add1 (.A(A), .B(B), .SUM(add1_sum));
  full_adder_1_bit_to_2_bit add2 (.A(C), .B(D), .SUM(add2_sum));
  full_adder_1_bit_to_2_bit add3 (.A(E), .B(F), .SUM(add3_sum));
  full_adder_1_bit_to_2_bit add4 (.A(G), .B(H), .SUM(add4_sum));
  full_adder_2bit_to_3_bit add5 (.A(add1_sum), .B(add2_sum), .SUM(add5_sum));
  full_adder_2bit_to_3_bit add6 (.A(add3_sum), .B(add4_sum), .SUM(add6_sum));
  full_adder_3_bit_to_4_bit add7 (.A(add5_sum), .B(add6_sum), .SUM(CNT));

  // Notes on the sheet:
  //   Popcount Implementation using my own adders instead of the build in adder
endmodule

module full_adder_2bit_to_3_bit (
  input  [1:0] A,
  input  [1:0] B,
  output [2:0] SUM
);

  wire adder1_carry;

  full_adder adder1 (.A(A[0]), .B(B[0]), .C_IN(1'b0), .SUM(SUM[0]), .CARRY(adder1_carry));
  full_adder adder2 (.A(A[1]), .B(B[1]), .C_IN(adder1_carry), .SUM(SUM[1]), .CARRY(SUM[2]));
endmodule

module full_adder_1_bit_to_2_bit (
  input  A,
  input  B,
  output [1:0] SUM
);

  full_adder adder (.A(A), .B(B), .C_IN(1'b0), .SUM(SUM[0]), .CARRY(SUM[1]));
endmodule

module full_adder_3_bit_to_4_bit (
  input  [2:0] A,
  input  [2:0] B,
  output [3:0] SUM
);

  wire adder1_carry, adder2_carry;

  full_adder adder1 (.A(A[0]), .B(B[0]), .C_IN(1'b0), .SUM(SUM[0]), .CARRY(adder1_carry));
  full_adder adder2 (.A(A[1]), .B(B[1]), .C_IN(adder1_carry), .SUM(SUM[1]), .CARRY(adder2_carry));
  full_adder adder3 (.A(A[2]), .B(B[2]), .C_IN(adder2_carry), .SUM(SUM[2]), .CARRY(SUM[3]));
endmodule

module single_cell (
  input  ME,
  input  NE,
  input  N,
  input  NW,
  input  W,
  input  E,
  input  SW,
  input  S,
  input  SE,
  output ME_N,
  output ME_S,
  output ME_E,
  output ME_W,
  output ALIVE
);

  wire and_1_out, and_2_out, comparator_1_eq, comparator_2_eq, or_1_out;
  wire [3:0] counter_cnt;

  popcount counter (.A(NE), .B(N), .C(NW), .D(W), .E(E), .F(SW), .G(S), .H(SE), .CNT(counter_cnt));
  Comparator #(.mode("unsigned"), .width(4)) comparator_1 (
    .a(counter_cnt), .b(4'b0010), .eq(comparator_1_eq));  // open: gt, lt
  Comparator #(.mode("unsigned"), .width(4)) comparator_2 (
    .a(counter_cnt), .b(4'b0011), .eq(comparator_2_eq));  // open: gt, lt
  or or_1 (or_1_out, comparator_1_eq, comparator_2_eq);
  and and_1 (and_1_out, ME, or_1_out);
  and and_2 (and_2_out, ~ME, comparator_2_eq);  // AND_Gate
  or or_2 (ALIVE, and_1_out, and_2_out);

  assign ME_E = ME;
  assign ME_N = ME;
  assign ME_S = ME;
  assign ME_W = ME;

  // Notes on the sheet:
  //   Rule 2: If alive and 2 or 3 Neighbors lives
  //   Rule 4: If dead and 3 neighbors, lives (reproduction)
  //   Rule 1: If alive and less than 2 Neighbors dies (Underpopulation)
  //   Rule 3: If alive and more than 3 neighbors dies (overpopulation)
  //   We only need to output value based on if we are alive or not. So we can exclude rules 1 and 3 from calculation
  //   Rule 2
  //   Rule 4
endmodule

module main (
  input  LOAD_RUN,
  input  CLK_EN,
  input  RESET
);

  wire and_1_out, CLK_out;
  wire [7:0] IN_ROW_1_sw8, IN_ROW_2_sw8, IN_ROW_3_sw8, IN_ROW_4_sw8, IN_ROW_5_sw8, IN_ROW_6_sw8,
       IN_ROW_7_sw8, IN_ROW_8_sw8;
  wire [63:0] cell_grid_1_grid_out, system_memory_1_mem_out;

  DipSwitch IN_ROW_1 (
    .sw1(IN_ROW_1_sw8[7]), .sw2(IN_ROW_1_sw8[6]), .sw3(IN_ROW_1_sw8[5]), .sw4(IN_ROW_1_sw8[4]),
    .sw5(IN_ROW_1_sw8[3]), .sw6(IN_ROW_1_sw8[2]), .sw7(IN_ROW_1_sw8[1]), .sw8(IN_ROW_1_sw8[0]));
  DipSwitch IN_ROW_2 (
    .sw1(IN_ROW_2_sw8[7]), .sw2(IN_ROW_2_sw8[6]), .sw3(IN_ROW_2_sw8[5]), .sw4(IN_ROW_2_sw8[4]),
    .sw5(IN_ROW_2_sw8[3]), .sw6(IN_ROW_2_sw8[2]), .sw7(IN_ROW_2_sw8[1]), .sw8(IN_ROW_2_sw8[0]));
  DipSwitch IN_ROW_3 (
    .sw1(IN_ROW_3_sw8[7]), .sw2(IN_ROW_3_sw8[6]), .sw3(IN_ROW_3_sw8[5]), .sw4(IN_ROW_3_sw8[4]),
    .sw5(IN_ROW_3_sw8[3]), .sw6(IN_ROW_3_sw8[2]), .sw7(IN_ROW_3_sw8[1]), .sw8(IN_ROW_3_sw8[0]));
  DipSwitch IN_ROW_4 (
    .sw1(IN_ROW_4_sw8[7]), .sw2(IN_ROW_4_sw8[6]), .sw3(IN_ROW_4_sw8[5]), .sw4(IN_ROW_4_sw8[4]),
    .sw5(IN_ROW_4_sw8[3]), .sw6(IN_ROW_4_sw8[2]), .sw7(IN_ROW_4_sw8[1]), .sw8(IN_ROW_4_sw8[0]));
  DipSwitch IN_ROW_5 (
    .sw1(IN_ROW_5_sw8[7]), .sw2(IN_ROW_5_sw8[6]), .sw3(IN_ROW_5_sw8[5]), .sw4(IN_ROW_5_sw8[4]),
    .sw5(IN_ROW_5_sw8[3]), .sw6(IN_ROW_5_sw8[2]), .sw7(IN_ROW_5_sw8[1]), .sw8(IN_ROW_5_sw8[0]));
  DipSwitch IN_ROW_6 (
    .sw1(IN_ROW_6_sw8[7]), .sw2(IN_ROW_6_sw8[6]), .sw3(IN_ROW_6_sw8[5]), .sw4(IN_ROW_6_sw8[4]),
    .sw5(IN_ROW_6_sw8[3]), .sw6(IN_ROW_6_sw8[2]), .sw7(IN_ROW_6_sw8[1]), .sw8(IN_ROW_6_sw8[0]));
  DipSwitch IN_ROW_7 (
    .sw1(IN_ROW_7_sw8[7]), .sw2(IN_ROW_7_sw8[6]), .sw3(IN_ROW_7_sw8[5]), .sw4(IN_ROW_7_sw8[4]),
    .sw5(IN_ROW_7_sw8[3]), .sw6(IN_ROW_7_sw8[2]), .sw7(IN_ROW_7_sw8[1]), .sw8(IN_ROW_7_sw8[0]));
  DipSwitch IN_ROW_8 (
    .sw1(IN_ROW_8_sw8[7]), .sw2(IN_ROW_8_sw8[6]), .sw3(IN_ROW_8_sw8[5]), .sw4(IN_ROW_8_sw8[4]),
    .sw5(IN_ROW_8_sw8[3]), .sw6(IN_ROW_8_sw8[2]), .sw7(IN_ROW_8_sw8[1]), .sw8(IN_ROW_8_sw8[0]));
  Clock CLK (.out(CLK_out));
  and and_1 (and_1_out, CLK_EN, CLK_out);
  // Probe on {IN_ROW_8_sw8, IN_ROW_7_sw8, IN_ROW_6_sw8, IN_ROW_5_sw8, IN_ROW_4_sw8, IN_ROW_3_sw8, IN_ROW_2_sw8, IN_ROW_1_sw8}
  // Probe on cell_grid_1_grid_out
  system_memory system_memory_1 (
    .GRID_IN(cell_grid_1_grid_out),
    .INITIAL_IN({IN_ROW_8_sw8, IN_ROW_7_sw8, IN_ROW_6_sw8, IN_ROW_5_sw8, IN_ROW_4_sw8, IN_ROW_3_sw8, IN_ROW_2_sw8, IN_ROW_1_sw8}),
    .WRITE_ENABLE(1'b1), .LOAD_RUN(LOAD_RUN), .CLK(and_1_out), .RESET(RESET),
    .MEM_OUT(system_memory_1_mem_out));
  DotMatrix #(.inputtype("row"), .matrixcols(8), .matrixrows(8)) INPUT_DISPLAY (
    .row0(system_memory_1_mem_out[7:0]), .row1(system_memory_1_mem_out[15:8]),
    .row2(system_memory_1_mem_out[23:16]), .row3(system_memory_1_mem_out[31:24]),
    .row4(system_memory_1_mem_out[39:32]), .row5(system_memory_1_mem_out[47:40]),
    .row6(system_memory_1_mem_out[55:48]), .row7(system_memory_1_mem_out[63:56]));
  cell_grid cell_grid_1 (.GRID_IN(system_memory_1_mem_out), .GRID_OUT(cell_grid_1_grid_out));
  DotMatrix #(.inputtype("row"), .matrixcols(8), .matrixrows(8)) OUTPUT_DISPLAY (
    .row0(cell_grid_1_grid_out[7:0]), .row1(cell_grid_1_grid_out[15:8]), .row2(cell_grid_1_grid_out[23:16]),
    .row3(cell_grid_1_grid_out[31:24]), .row4(cell_grid_1_grid_out[39:32]),
    .row5(cell_grid_1_grid_out[47:40]), .row6(cell_grid_1_grid_out[55:48]), .row7(cell_grid_1_grid_out[63:56]));

  // Notes on the sheet:
  //   1. Set in your initial value using the DIP switches
  //   2. Set CLK_EN to true and cycle CLK once to load memory
  //   3. Set LOAD_RUN to start running the proces
  //   4. Keep cycling CLK to run through the process
endmodule

module single_cell_TTL (
  input  ME,
  input  NE,
  input  N,
  input  NW,
  input  W,
  input  E,
  input  SW,
  input  S,
  input  SE,
  output ME_N,
  output ME_S,
  output ME_E,
  output ME_W,
  output ALIVE
);

  wire dual_comparator_ttl_1_ab_equal, dual_comparator_ttl_1_cd_equal, n7404_1_pin12, n7432_1_pin8;
  wire [3:0] COUNTER_count1;

  popcount_TTL COUNTER (
    .A(NE), .B(N), .C(NW), .D(W), .E(E), .F(SW), .G(S), .H(SE), .COUNT1(COUNTER_count1[0]),
    .COUNT2(COUNTER_count1[1]), .COUNT3(COUNTER_count1[2]), .COUNT4(COUNTER_count1[3]));
  dual_comparator_TTL dual_comparator_ttl_1 (
    .A(COUNTER_count1), .B(4'b0010), .C(COUNTER_count1), .D(4'b0011),
    .AB_EQUAL(dual_comparator_ttl_1_ab_equal), .CD_EQUAL(dual_comparator_ttl_1_cd_equal));
  _7432 u_7432_1 (
    .pin10(dual_comparator_ttl_1_cd_equal), .pin9(dual_comparator_ttl_1_ab_equal), .pin8(n7432_1_pin8));  // open: pin1, pin2, pin3, pin4, pin5, pin6, pin13, pin12, pin11
  _7404 u_7404_1 (
    .pin13(ME), .pin12(n7404_1_pin12));  // open: pin1, pin2, pin3, pin4, pin5, pin6, pin11, pin10, pin9, pin8
  _7458 u_7458_1 (
    .pin2(ME), .pin3(n7432_1_pin8), .pin4(dual_comparator_ttl_1_cd_equal), .pin5(n7404_1_pin12), .pin6(ALIVE));  // open: pin1, pin13, pin12, pin11, pin10, pin9, pin8

  assign ME_E = ME;
  assign ME_N = ME;
  assign ME_S = ME;
  assign ME_W = ME;

  // Notes on the sheet:
  //   Rule 2: If alive and 2 or 3 Neighbors lives
  //   Rule 4: If dead and 3 neighbors, lives (reproduction)
  //   Rule 1: If alive and less than 2 Neighbors dies (Underpopulation)
  //   Rule 3: If alive and more than 3 neighbors dies (overpopulation)
  //   We only need to output value based on if we are alive or not. So we can exclude rules 1 and 3 from calculation
  //   OR gate can be shared between 4 cells
  //   Rule 2
  //   Rule 4
  //   NOT gate can be shared between 4 cells
  //   AND-OR chip. Can be shared between 2 cells. 
  //   Since second side is 3 input, 3rd inputs should be tied to VCC
endmodule

module popcount_TTL (
  input  A,
  input  B,
  input  C,
  input  D,
  input  E,
  input  F,
  input  G,
  input  H,
  output COUNT1,
  output COUNT2,
  output COUNT3,
  output COUNT4
);

  wire n74283_1_pin1, n74283_1_pin4, n74283_1_pin10, n74283_1_pin13, n74283_2_pin1, n74283_2_pin4,
       n74283_2_pin10, n74283_2_pin13, n74283_3_pin1, n74283_3_pin4, n74283_3_pin13, n74283_4_pin1,
       n74283_4_pin4, n74283_4_pin13;

  _74283 u_74283_1 (
    .pin1(n74283_1_pin1), .pin4(n74283_1_pin4), .pin5(A), .pin6(B), .pin15(D), .pin14(C),
    .pin13(n74283_1_pin13), .pin10(n74283_1_pin10));  // open: pin2, pin3, pin7, pin12, pin11, pin9
  _74283 u_74283_2 (
    .pin1(n74283_2_pin1), .pin4(n74283_2_pin4), .pin5(E), .pin6(F), .pin15(H), .pin14(G),
    .pin13(n74283_2_pin13), .pin10(n74283_2_pin10));  // open: pin2, pin3, pin7, pin12, pin11, pin9
  _74283 u_74283_3 (
    .pin1(n74283_3_pin1), .pin2(n74283_2_pin10), .pin3(n74283_2_pin1), .pin4(n74283_3_pin4),
    .pin5(n74283_2_pin4), .pin6(n74283_2_pin13), .pin13(n74283_3_pin13));  // open: pin7, pin15, pin14, pin12, pin11, pin10, pin9
  _74283 u_74283_4 (
    .pin1(n74283_4_pin1), .pin2(n74283_1_pin10), .pin3(n74283_1_pin1), .pin4(n74283_4_pin4),
    .pin5(n74283_1_pin4), .pin6(n74283_1_pin13), .pin13(n74283_4_pin13));  // open: pin7, pin15, pin14, pin12, pin11, pin10, pin9
  _74283 u_74283_5 (
    .pin1(COUNT2), .pin2(n74283_3_pin1), .pin3(n74283_4_pin1), .pin4(COUNT1), .pin5(n74283_4_pin4),
    .pin6(n74283_3_pin4), .pin15(n74283_3_pin13), .pin14(n74283_4_pin13), .pin13(COUNT3), .pin10(COUNT4));  // open: pin7, pin12, pin11, pin9

  // Notes on the sheet:
  //   The 74283 is a 4 bit adder. But since we never are adding more than 1+1, we can use it as 2x2bit adders for the first stage
endmodule

module dual_comparator_TTL (
  input  [3:0] A,
  input  [3:0] B,
  input  [3:0] C,
  input  [3:0] D,
  output AB_EQUAL,
  output CD_EQUAL
);

  wire n747266_1_pin3, n747266_1_pin6, n747266_1_pin8, n747266_1_pin11, n747266_2_pin3, n747266_2_pin6,
       n747266_2_pin8, n747266_2_pin11;

  _747266 u_747266_1 (
    .pin1(B[3]), .pin2(A[2]), .pin3(n747266_1_pin3), .pin4(B[2]), .pin5(A[3]), .pin6(n747266_1_pin6),
    .pin13(B[0]), .pin12(A[0]), .pin11(n747266_1_pin11), .pin10(B[1]), .pin9(A[1]), .pin8(n747266_1_pin8));
  _747266 u_747266_2 (
    .pin1(D[3]), .pin2(C[2]), .pin3(n747266_2_pin3), .pin4(D[2]), .pin5(C[3]), .pin6(n747266_2_pin6),
    .pin13(D[0]), .pin12(C[0]), .pin11(n747266_2_pin11), .pin10(D[1]), .pin9(C[1]), .pin8(n747266_2_pin8));
  _7421 #(.ShowInternalStructure("true")) u_7421_1 (
    .pin1(n747266_2_pin11), .pin2(n747266_2_pin8), .pin4(n747266_2_pin6), .pin5(n747266_2_pin3),
    .pin6(CD_EQUAL), .pin13(n747266_1_pin3), .pin12(n747266_1_pin6), .pin10(n747266_1_pin8),
    .pin9(n747266_1_pin11), .pin8(AB_EQUAL));  // open: pin3, pin11
endmodule

module single_cell_memory (
  input  ME_INIT,
  input  SET,
  input  CLK,
  input  NE,
  input  N,
  input  NW,
  input  W,
  input  E,
  input  SW,
  input  S,
  input  SE,
  output ME_N,
  output ME_S,
  output ME_E,
  output ME_W,
  output ALIVE
);

  wire and_1_out, and_2_out, comparator_1_eq, comparator_2_eq, multiplexer_1_out, or_1_out;
  wire [3:0] counter_cnt;

  D_Flip_Flop d_ff_1 (.D(multiplexer_1_out), .clk(CLK), .Q(ME_E));  // open: Qn, preset, reset
  Multiplexer multiplexer_1 (.in0(ALIVE), .in1(ME_INIT), .out(multiplexer_1_out), .sel(SET));
  popcount counter (.A(NE), .B(N), .C(NW), .D(W), .E(E), .F(SW), .G(S), .H(SE), .CNT(counter_cnt));
  Comparator #(.mode("unsigned"), .width(4)) comparator_1 (
    .a(counter_cnt), .b(4'b0010), .eq(comparator_1_eq));  // open: gt, lt
  Comparator #(.mode("unsigned"), .width(4)) comparator_2 (
    .a(counter_cnt), .b(4'b0011), .eq(comparator_2_eq));  // open: gt, lt
  or or_1 (or_1_out, comparator_1_eq, comparator_2_eq);
  and and_1 (and_1_out, ME_E, or_1_out);
  and and_2 (and_2_out, ~ME_E, comparator_2_eq);  // AND_Gate
  or or_2 (ALIVE, and_1_out, and_2_out);

  assign ME_N = ME_E;
  assign ME_S = ME_E;
  assign ME_W = ME_E;

  // Notes on the sheet:
  //   This is a version of "single_cell", but with the memory of the state stored internally
  //   When "SET" is asserted, next clock will set internal memory from ME_INIT
  //   Rule 2: If alive and 2 or 3 Neighbors lives
  //   Rule 1: If alive and less than 2 Neighbors dies (Underpopulation)
  //   Rule 3: If alive and more than 3 neighbors dies (overpopulation)
  //   Rule 4: If dead and 3 neighbors, lives (reproduction)
  //   We only need to output value based on if we are alive or not. So we can exclude rules 1 and 3 from calculation
  //   Rule 2
  //   Rule 4
endmodule

module cell_grid (
  input  [63:0] GRID_IN,
  output [63:0] GRID_OUT
);

  wire CELL_0_0_me_e, CELL_0_0_me_s, CELL_0_1_me_e, CELL_0_1_me_s, CELL_0_1_me_w, CELL_0_2_me_e,
       CELL_0_2_me_s, CELL_0_2_me_w, CELL_0_3_me_e, CELL_0_3_me_s, CELL_0_3_me_w, CELL_0_4_me_e,
       CELL_0_4_me_s, CELL_0_4_me_w, CELL_0_5_me_e, CELL_0_5_me_s, CELL_0_5_me_w, CELL_0_6_me_e,
       CELL_0_6_me_s, CELL_0_6_me_w, CELL_0_7_me_s, CELL_0_7_me_w, CELL_1_0_me_e, CELL_1_0_me_n,
       CELL_1_0_me_s, CELL_1_1_me_e, CELL_1_1_me_n, CELL_1_1_me_s, CELL_1_1_me_w, CELL_1_2_me_e,
       CELL_1_2_me_n, CELL_1_2_me_s, CELL_1_2_me_w, CELL_1_3_me_e, CELL_1_3_me_n, CELL_1_3_me_s,
       CELL_1_3_me_w, CELL_1_4_me_e, CELL_1_4_me_n, CELL_1_4_me_s, CELL_1_4_me_w, CELL_1_5_me_e,
       CELL_1_5_me_n, CELL_1_5_me_s, CELL_1_5_me_w, CELL_1_6_me_e, CELL_1_6_me_n, CELL_1_6_me_s,
       CELL_1_6_me_w, CELL_1_7_me_n, CELL_1_7_me_s, CELL_1_7_me_w, CELL_2_0_me_e, CELL_2_0_me_n,
       CELL_2_0_me_s, CELL_2_1_me_e, CELL_2_1_me_n, CELL_2_1_me_s, CELL_2_1_me_w, CELL_2_2_me_e,
       CELL_2_2_me_n, CELL_2_2_me_s, CELL_2_2_me_w, CELL_2_3_me_e, CELL_2_3_me_n, CELL_2_3_me_s,
       CELL_2_3_me_w, CELL_2_4_me_e, CELL_2_4_me_n, CELL_2_4_me_s, CELL_2_4_me_w, CELL_2_5_me_e,
       CELL_2_5_me_n, CELL_2_5_me_s, CELL_2_5_me_w, CELL_2_6_me_e, CELL_2_6_me_n, CELL_2_6_me_s,
       CELL_2_6_me_w, CELL_2_7_me_n, CELL_2_7_me_s, CELL_2_7_me_w, CELL_3_0_me_e, CELL_3_0_me_n,
       CELL_3_0_me_s, CELL_3_1_me_e, CELL_3_1_me_n, CELL_3_1_me_s, CELL_3_1_me_w, CELL_3_2_me_e,
       CELL_3_2_me_n, CELL_3_2_me_s, CELL_3_2_me_w, CELL_3_3_me_e, CELL_3_3_me_n, CELL_3_3_me_s,
       CELL_3_3_me_w, CELL_3_4_me_e, CELL_3_4_me_n, CELL_3_4_me_s, CELL_3_4_me_w, CELL_3_5_me_e,
       CELL_3_5_me_n, CELL_3_5_me_s, CELL_3_5_me_w, CELL_3_6_me_e, CELL_3_6_me_n, CELL_3_6_me_s,
       CELL_3_6_me_w, CELL_3_7_me_n, CELL_3_7_me_s, CELL_3_7_me_w, CELL_4_0_me_e, CELL_4_0_me_n,
       CELL_4_0_me_s, CELL_4_1_me_e, CELL_4_1_me_n, CELL_4_1_me_s, CELL_4_1_me_w, CELL_4_2_me_e,
       CELL_4_2_me_n, CELL_4_2_me_s, CELL_4_2_me_w, CELL_4_3_me_e, CELL_4_3_me_n, CELL_4_3_me_s,
       CELL_4_3_me_w, CELL_4_4_me_e, CELL_4_4_me_n, CELL_4_4_me_s, CELL_4_4_me_w, CELL_4_5_me_e,
       CELL_4_5_me_n, CELL_4_5_me_s, CELL_4_5_me_w, CELL_4_6_me_e, CELL_4_6_me_n, CELL_4_6_me_s,
       CELL_4_6_me_w, CELL_4_7_me_n, CELL_4_7_me_s, CELL_4_7_me_w, CELL_5_0_me_e, CELL_5_0_me_n,
       CELL_5_0_me_s, CELL_5_1_me_e, CELL_5_1_me_n, CELL_5_1_me_s, CELL_5_1_me_w, CELL_5_2_me_e,
       CELL_5_2_me_n, CELL_5_2_me_s, CELL_5_2_me_w, CELL_5_3_me_e, CELL_5_3_me_n, CELL_5_3_me_s,
       CELL_5_3_me_w, CELL_5_4_me_e, CELL_5_4_me_n, CELL_5_4_me_s, CELL_5_4_me_w, CELL_5_5_me_e,
       CELL_5_5_me_n, CELL_5_5_me_s, CELL_5_5_me_w, CELL_5_6_me_e, CELL_5_6_me_n, CELL_5_6_me_s,
       CELL_5_6_me_w, CELL_5_7_me_n, CELL_5_7_me_s, CELL_5_7_me_w, CELL_6_0_me_e, CELL_6_0_me_n,
       CELL_6_0_me_s, CELL_6_1_me_e, CELL_6_1_me_n, CELL_6_1_me_s, CELL_6_1_me_w, CELL_6_2_me_e,
       CELL_6_2_me_n, CELL_6_2_me_s, CELL_6_2_me_w, CELL_6_3_me_e, CELL_6_3_me_n, CELL_6_3_me_s,
       CELL_6_3_me_w, CELL_6_4_me_e, CELL_6_4_me_n, CELL_6_4_me_s, CELL_6_4_me_w, CELL_6_5_me_e,
       CELL_6_5_me_n, CELL_6_5_me_s, CELL_6_5_me_w, CELL_6_6_me_e, CELL_6_6_me_n, CELL_6_6_me_s,
       CELL_6_6_me_w, CELL_6_7_me_n, CELL_6_7_me_s, CELL_6_7_me_w, CELL_7_0_me_e, CELL_7_0_me_n,
       CELL_7_1_me_e, CELL_7_1_me_n, CELL_7_1_me_w, CELL_7_2_me_e, CELL_7_2_me_n, CELL_7_2_me_w,
       CELL_7_3_me_e, CELL_7_3_me_n, CELL_7_3_me_w, CELL_7_4_me_e, CELL_7_4_me_n, CELL_7_4_me_w,
       CELL_7_5_me_e, CELL_7_5_me_n, CELL_7_5_me_w, CELL_7_6_me_e, CELL_7_6_me_n, CELL_7_6_me_w,
       CELL_7_7_me_n, CELL_7_7_me_w;

  single_cell CELL_0_0 (
    .E(CELL_0_1_me_w), .S(CELL_1_0_me_n), .SE(CELL_1_1_me_n), .ME(GRID_IN[0]), .ALIVE(GRID_OUT[0]),
    .ME_S(CELL_0_0_me_s), .ME_E(CELL_0_0_me_e));  // open: NE, N, NW, W, SW, ME_N, ME_W
  single_cell CELL_1_0 (
    .NE(CELL_0_1_me_s), .N(CELL_0_0_me_s), .E(CELL_1_1_me_w), .S(CELL_2_0_me_n), .SE(CELL_2_1_me_n),
    .ME(GRID_IN[8]), .ALIVE(GRID_OUT[8]), .ME_N(CELL_1_0_me_n), .ME_S(CELL_1_0_me_s), .ME_E(CELL_1_0_me_e));  // open: NW, W, SW, ME_W
  single_cell CELL_2_0 (
    .NE(CELL_1_1_me_s), .N(CELL_1_0_me_s), .E(CELL_2_1_me_w), .S(CELL_3_0_me_n), .SE(CELL_3_1_me_n),
    .ME(GRID_IN[16]), .ALIVE(GRID_OUT[16]), .ME_N(CELL_2_0_me_n), .ME_S(CELL_2_0_me_s), .ME_E(CELL_2_0_me_e));  // open: NW, W, SW, ME_W
  single_cell CELL_3_0 (
    .NE(CELL_2_1_me_s), .N(CELL_2_0_me_s), .E(CELL_3_1_me_w), .S(CELL_4_0_me_n), .SE(CELL_4_1_me_n),
    .ME(GRID_IN[24]), .ALIVE(GRID_OUT[24]), .ME_N(CELL_3_0_me_n), .ME_S(CELL_3_0_me_s), .ME_E(CELL_3_0_me_e));  // open: NW, W, SW, ME_W
  single_cell CELL_4_0 (
    .NE(CELL_3_1_me_s), .N(CELL_3_0_me_s), .E(CELL_4_1_me_w), .S(CELL_5_0_me_n), .SE(CELL_5_1_me_n),
    .ME(GRID_IN[32]), .ALIVE(GRID_OUT[32]), .ME_N(CELL_4_0_me_n), .ME_S(CELL_4_0_me_s), .ME_E(CELL_4_0_me_e));  // open: NW, W, SW, ME_W
  single_cell CELL_5_0 (
    .NE(CELL_4_1_me_s), .N(CELL_4_0_me_s), .E(CELL_5_1_me_w), .S(CELL_6_0_me_n), .SE(CELL_6_1_me_n),
    .ME(GRID_IN[40]), .ALIVE(GRID_OUT[40]), .ME_N(CELL_5_0_me_n), .ME_S(CELL_5_0_me_s), .ME_E(CELL_5_0_me_e));  // open: NW, W, SW, ME_W
  single_cell CELL_6_0 (
    .NE(CELL_5_1_me_s), .N(CELL_5_0_me_s), .E(CELL_6_1_me_w), .S(CELL_7_0_me_n), .SE(CELL_7_1_me_n),
    .ME(GRID_IN[48]), .ALIVE(GRID_OUT[48]), .ME_N(CELL_6_0_me_n), .ME_S(CELL_6_0_me_s), .ME_E(CELL_6_0_me_e));  // open: NW, W, SW, ME_W
  single_cell CELL_7_0 (
    .NE(CELL_6_1_me_s), .N(CELL_6_0_me_s), .E(CELL_7_1_me_w), .ME(GRID_IN[56]), .ALIVE(GRID_OUT[56]),
    .ME_N(CELL_7_0_me_n), .ME_E(CELL_7_0_me_e));  // open: NW, W, SW, S, SE, ME_S, ME_W
  single_cell CELL_0_1 (
    .W(CELL_0_0_me_e), .E(CELL_0_2_me_w), .SW(CELL_1_0_me_n), .S(CELL_1_1_me_n), .SE(CELL_1_2_me_n),
    .ME(GRID_IN[1]), .ALIVE(GRID_OUT[1]), .ME_S(CELL_0_1_me_s), .ME_E(CELL_0_1_me_e), .ME_W(CELL_0_1_me_w));  // open: NE, N, NW, ME_N
  single_cell CELL_1_1 (
    .NE(CELL_0_2_me_s), .N(CELL_0_1_me_s), .NW(CELL_0_0_me_s), .W(CELL_1_0_me_e), .E(CELL_1_2_me_w),
    .SW(CELL_2_0_me_n), .S(CELL_2_1_me_n), .SE(CELL_2_2_me_n), .ME(GRID_IN[9]), .ALIVE(GRID_OUT[9]),
    .ME_N(CELL_1_1_me_n), .ME_S(CELL_1_1_me_s), .ME_E(CELL_1_1_me_e), .ME_W(CELL_1_1_me_w));
  single_cell CELL_2_1 (
    .NE(CELL_1_2_me_s), .N(CELL_1_1_me_s), .NW(CELL_1_0_me_s), .W(CELL_2_0_me_e), .E(CELL_2_2_me_w),
    .SW(CELL_3_0_me_n), .S(CELL_3_1_me_n), .SE(CELL_3_2_me_n), .ME(GRID_IN[17]), .ALIVE(GRID_OUT[17]),
    .ME_N(CELL_2_1_me_n), .ME_S(CELL_2_1_me_s), .ME_E(CELL_2_1_me_e), .ME_W(CELL_2_1_me_w));
  single_cell CELL_3_1 (
    .NE(CELL_2_2_me_s), .N(CELL_2_1_me_s), .NW(CELL_2_0_me_s), .W(CELL_3_0_me_e), .E(CELL_3_2_me_w),
    .SW(CELL_4_0_me_n), .S(CELL_4_1_me_n), .SE(CELL_4_2_me_n), .ME(GRID_IN[25]), .ALIVE(GRID_OUT[25]),
    .ME_N(CELL_3_1_me_n), .ME_S(CELL_3_1_me_s), .ME_E(CELL_3_1_me_e), .ME_W(CELL_3_1_me_w));
  single_cell CELL_4_1 (
    .NE(CELL_3_2_me_s), .N(CELL_3_1_me_s), .NW(CELL_3_0_me_s), .W(CELL_4_0_me_e), .E(CELL_4_2_me_w),
    .SW(CELL_5_0_me_n), .S(CELL_5_1_me_n), .SE(CELL_5_2_me_n), .ME(GRID_IN[33]), .ALIVE(GRID_OUT[33]),
    .ME_N(CELL_4_1_me_n), .ME_S(CELL_4_1_me_s), .ME_E(CELL_4_1_me_e), .ME_W(CELL_4_1_me_w));
  single_cell CELL_5_1 (
    .NE(CELL_4_2_me_s), .N(CELL_4_1_me_s), .NW(CELL_4_0_me_s), .W(CELL_5_0_me_e), .E(CELL_5_2_me_w),
    .SW(CELL_6_0_me_n), .S(CELL_6_1_me_n), .SE(CELL_6_2_me_n), .ME(GRID_IN[41]), .ALIVE(GRID_OUT[41]),
    .ME_N(CELL_5_1_me_n), .ME_S(CELL_5_1_me_s), .ME_E(CELL_5_1_me_e), .ME_W(CELL_5_1_me_w));
  single_cell CELL_6_1 (
    .NE(CELL_5_2_me_s), .N(CELL_5_1_me_s), .NW(CELL_5_0_me_s), .W(CELL_6_0_me_e), .E(CELL_6_2_me_w),
    .SW(CELL_7_0_me_n), .S(CELL_7_1_me_n), .SE(CELL_7_2_me_n), .ME(GRID_IN[49]), .ALIVE(GRID_OUT[49]),
    .ME_N(CELL_6_1_me_n), .ME_S(CELL_6_1_me_s), .ME_E(CELL_6_1_me_e), .ME_W(CELL_6_1_me_w));
  single_cell CELL_7_1 (
    .NE(CELL_6_2_me_s), .N(CELL_6_1_me_s), .NW(CELL_6_0_me_s), .W(CELL_7_0_me_e), .E(CELL_7_2_me_w),
    .ME(GRID_IN[57]), .ALIVE(GRID_OUT[57]), .ME_N(CELL_7_1_me_n), .ME_E(CELL_7_1_me_e), .ME_W(CELL_7_1_me_w));  // open: SW, S, SE, ME_S
  single_cell CELL_0_2 (
    .W(CELL_0_1_me_e), .E(CELL_0_3_me_w), .SW(CELL_1_1_me_n), .S(CELL_1_2_me_n), .SE(CELL_1_3_me_n),
    .ME(GRID_IN[2]), .ALIVE(GRID_OUT[2]), .ME_S(CELL_0_2_me_s), .ME_E(CELL_0_2_me_e), .ME_W(CELL_0_2_me_w));  // open: NE, N, NW, ME_N
  single_cell CELL_1_2 (
    .NE(CELL_0_3_me_s), .N(CELL_0_2_me_s), .NW(CELL_0_1_me_s), .W(CELL_1_1_me_e), .E(CELL_1_3_me_w),
    .SW(CELL_2_1_me_n), .S(CELL_2_2_me_n), .SE(CELL_2_3_me_n), .ME(GRID_IN[10]), .ALIVE(GRID_OUT[10]),
    .ME_N(CELL_1_2_me_n), .ME_S(CELL_1_2_me_s), .ME_E(CELL_1_2_me_e), .ME_W(CELL_1_2_me_w));
  single_cell CELL_2_2 (
    .NE(CELL_1_3_me_s), .N(CELL_1_2_me_s), .NW(CELL_1_1_me_s), .W(CELL_2_1_me_e), .E(CELL_2_3_me_w),
    .SW(CELL_3_1_me_n), .S(CELL_3_2_me_n), .SE(CELL_3_3_me_n), .ME(GRID_IN[18]), .ALIVE(GRID_OUT[18]),
    .ME_N(CELL_2_2_me_n), .ME_S(CELL_2_2_me_s), .ME_E(CELL_2_2_me_e), .ME_W(CELL_2_2_me_w));
  single_cell CELL_3_2 (
    .NE(CELL_2_3_me_s), .N(CELL_2_2_me_s), .NW(CELL_2_1_me_s), .W(CELL_3_1_me_e), .E(CELL_3_3_me_w),
    .SW(CELL_4_1_me_n), .S(CELL_4_2_me_n), .SE(CELL_4_3_me_n), .ME(GRID_IN[26]), .ALIVE(GRID_OUT[26]),
    .ME_N(CELL_3_2_me_n), .ME_S(CELL_3_2_me_s), .ME_E(CELL_3_2_me_e), .ME_W(CELL_3_2_me_w));
  single_cell CELL_4_2 (
    .NE(CELL_3_3_me_s), .N(CELL_3_2_me_s), .NW(CELL_3_1_me_s), .W(CELL_4_1_me_e), .E(CELL_4_3_me_w),
    .SW(CELL_5_1_me_n), .S(CELL_5_2_me_n), .SE(CELL_5_3_me_n), .ME(GRID_IN[34]), .ALIVE(GRID_OUT[34]),
    .ME_N(CELL_4_2_me_n), .ME_S(CELL_4_2_me_s), .ME_E(CELL_4_2_me_e), .ME_W(CELL_4_2_me_w));
  single_cell CELL_5_2 (
    .NE(CELL_4_3_me_s), .N(CELL_4_2_me_s), .NW(CELL_4_1_me_s), .W(CELL_5_1_me_e), .E(CELL_5_3_me_w),
    .SW(CELL_6_1_me_n), .S(CELL_6_2_me_n), .SE(CELL_6_3_me_n), .ME(GRID_IN[42]), .ALIVE(GRID_OUT[42]),
    .ME_N(CELL_5_2_me_n), .ME_S(CELL_5_2_me_s), .ME_E(CELL_5_2_me_e), .ME_W(CELL_5_2_me_w));
  single_cell CELL_6_2 (
    .NE(CELL_5_3_me_s), .N(CELL_5_2_me_s), .NW(CELL_5_1_me_s), .W(CELL_6_1_me_e), .E(CELL_6_3_me_w),
    .SW(CELL_7_1_me_n), .S(CELL_7_2_me_n), .SE(CELL_7_3_me_n), .ME(GRID_IN[50]), .ALIVE(GRID_OUT[50]),
    .ME_N(CELL_6_2_me_n), .ME_S(CELL_6_2_me_s), .ME_E(CELL_6_2_me_e), .ME_W(CELL_6_2_me_w));
  single_cell CELL_7_2 (
    .NE(CELL_6_3_me_s), .N(CELL_6_2_me_s), .NW(CELL_6_1_me_s), .W(CELL_7_1_me_e), .E(CELL_7_3_me_w),
    .ME(GRID_IN[58]), .ALIVE(GRID_OUT[58]), .ME_N(CELL_7_2_me_n), .ME_E(CELL_7_2_me_e), .ME_W(CELL_7_2_me_w));  // open: SW, S, SE, ME_S
  single_cell CELL_0_3 (
    .W(CELL_0_2_me_e), .E(CELL_0_4_me_w), .SW(CELL_1_2_me_n), .S(CELL_1_3_me_n), .SE(CELL_1_4_me_n),
    .ME(GRID_IN[3]), .ALIVE(GRID_OUT[3]), .ME_S(CELL_0_3_me_s), .ME_E(CELL_0_3_me_e), .ME_W(CELL_0_3_me_w));  // open: NE, N, NW, ME_N
  single_cell CELL_1_3 (
    .NE(CELL_0_4_me_s), .N(CELL_0_3_me_s), .NW(CELL_0_2_me_s), .W(CELL_1_2_me_e), .E(CELL_1_4_me_w),
    .SW(CELL_2_2_me_n), .S(CELL_2_3_me_n), .SE(CELL_2_4_me_n), .ME(GRID_IN[11]), .ALIVE(GRID_OUT[11]),
    .ME_N(CELL_1_3_me_n), .ME_S(CELL_1_3_me_s), .ME_E(CELL_1_3_me_e), .ME_W(CELL_1_3_me_w));
  single_cell CELL_2_3 (
    .NE(CELL_1_4_me_s), .N(CELL_1_3_me_s), .NW(CELL_1_2_me_s), .W(CELL_2_2_me_e), .E(CELL_2_4_me_w),
    .SW(CELL_3_2_me_n), .S(CELL_3_3_me_n), .SE(CELL_3_4_me_n), .ME(GRID_IN[19]), .ALIVE(GRID_OUT[19]),
    .ME_N(CELL_2_3_me_n), .ME_S(CELL_2_3_me_s), .ME_E(CELL_2_3_me_e), .ME_W(CELL_2_3_me_w));
  single_cell CELL_3_3 (
    .NE(CELL_2_4_me_s), .N(CELL_2_3_me_s), .NW(CELL_2_2_me_s), .W(CELL_3_2_me_e), .E(CELL_3_4_me_w),
    .SW(CELL_4_2_me_n), .S(CELL_4_3_me_n), .SE(CELL_4_4_me_n), .ME(GRID_IN[27]), .ALIVE(GRID_OUT[27]),
    .ME_N(CELL_3_3_me_n), .ME_S(CELL_3_3_me_s), .ME_E(CELL_3_3_me_e), .ME_W(CELL_3_3_me_w));
  single_cell CELL_4_3 (
    .NE(CELL_3_4_me_s), .N(CELL_3_3_me_s), .NW(CELL_3_2_me_s), .W(CELL_4_2_me_e), .E(CELL_4_4_me_w),
    .SW(CELL_5_2_me_n), .S(CELL_5_3_me_n), .SE(CELL_5_4_me_n), .ME(GRID_IN[35]), .ALIVE(GRID_OUT[35]),
    .ME_N(CELL_4_3_me_n), .ME_S(CELL_4_3_me_s), .ME_E(CELL_4_3_me_e), .ME_W(CELL_4_3_me_w));
  single_cell CELL_5_3 (
    .NE(CELL_4_4_me_s), .N(CELL_4_3_me_s), .NW(CELL_4_2_me_s), .W(CELL_5_2_me_e), .E(CELL_5_4_me_w),
    .SW(CELL_6_2_me_n), .S(CELL_6_3_me_n), .SE(CELL_6_4_me_n), .ME(GRID_IN[43]), .ALIVE(GRID_OUT[43]),
    .ME_N(CELL_5_3_me_n), .ME_S(CELL_5_3_me_s), .ME_E(CELL_5_3_me_e), .ME_W(CELL_5_3_me_w));
  single_cell CELL_6_3 (
    .NE(CELL_5_4_me_s), .N(CELL_5_3_me_s), .NW(CELL_5_2_me_s), .W(CELL_6_2_me_e), .E(CELL_6_4_me_w),
    .SW(CELL_7_2_me_n), .S(CELL_7_3_me_n), .SE(CELL_7_4_me_n), .ME(GRID_IN[51]), .ALIVE(GRID_OUT[51]),
    .ME_N(CELL_6_3_me_n), .ME_S(CELL_6_3_me_s), .ME_E(CELL_6_3_me_e), .ME_W(CELL_6_3_me_w));
  single_cell CELL_7_3 (
    .NE(CELL_6_4_me_s), .N(CELL_6_3_me_s), .NW(CELL_6_2_me_s), .W(CELL_7_2_me_e), .E(CELL_7_4_me_w),
    .ME(GRID_IN[59]), .ALIVE(GRID_OUT[59]), .ME_N(CELL_7_3_me_n), .ME_E(CELL_7_3_me_e), .ME_W(CELL_7_3_me_w));  // open: SW, S, SE, ME_S
  single_cell CELL_0_4 (
    .W(CELL_0_3_me_e), .E(CELL_0_5_me_w), .SW(CELL_1_3_me_n), .S(CELL_1_4_me_n), .SE(CELL_1_5_me_n),
    .ME(GRID_IN[4]), .ALIVE(GRID_OUT[4]), .ME_S(CELL_0_4_me_s), .ME_E(CELL_0_4_me_e), .ME_W(CELL_0_4_me_w));  // open: NE, N, NW, ME_N
  single_cell CELL_1_4 (
    .NE(CELL_0_5_me_s), .N(CELL_0_4_me_s), .NW(CELL_0_3_me_s), .W(CELL_1_3_me_e), .E(CELL_1_5_me_w),
    .SW(CELL_2_3_me_n), .S(CELL_2_4_me_n), .SE(CELL_2_5_me_n), .ME(GRID_IN[12]), .ALIVE(GRID_OUT[12]),
    .ME_N(CELL_1_4_me_n), .ME_S(CELL_1_4_me_s), .ME_E(CELL_1_4_me_e), .ME_W(CELL_1_4_me_w));
  single_cell CELL_2_4 (
    .NE(CELL_1_5_me_s), .N(CELL_1_4_me_s), .NW(CELL_1_3_me_s), .W(CELL_2_3_me_e), .E(CELL_2_5_me_w),
    .SW(CELL_3_3_me_n), .S(CELL_3_4_me_n), .SE(CELL_3_5_me_n), .ME(GRID_IN[20]), .ALIVE(GRID_OUT[20]),
    .ME_N(CELL_2_4_me_n), .ME_S(CELL_2_4_me_s), .ME_E(CELL_2_4_me_e), .ME_W(CELL_2_4_me_w));
  single_cell CELL_3_4 (
    .NE(CELL_2_5_me_s), .N(CELL_2_4_me_s), .NW(CELL_2_3_me_s), .W(CELL_3_3_me_e), .E(CELL_3_5_me_w),
    .SW(CELL_4_3_me_n), .S(CELL_4_4_me_n), .SE(CELL_4_5_me_n), .ME(GRID_IN[28]), .ALIVE(GRID_OUT[28]),
    .ME_N(CELL_3_4_me_n), .ME_S(CELL_3_4_me_s), .ME_E(CELL_3_4_me_e), .ME_W(CELL_3_4_me_w));
  single_cell CELL_4_4 (
    .NE(CELL_3_5_me_s), .N(CELL_3_4_me_s), .NW(CELL_3_3_me_s), .W(CELL_4_3_me_e), .E(CELL_4_5_me_w),
    .SW(CELL_5_3_me_n), .S(CELL_5_4_me_n), .SE(CELL_5_5_me_n), .ME(GRID_IN[36]), .ALIVE(GRID_OUT[36]),
    .ME_N(CELL_4_4_me_n), .ME_S(CELL_4_4_me_s), .ME_E(CELL_4_4_me_e), .ME_W(CELL_4_4_me_w));
  single_cell CELL_5_4 (
    .NE(CELL_4_5_me_s), .N(CELL_4_4_me_s), .NW(CELL_4_3_me_s), .W(CELL_5_3_me_e), .E(CELL_5_5_me_w),
    .SW(CELL_6_3_me_n), .S(CELL_6_4_me_n), .SE(CELL_6_5_me_n), .ME(GRID_IN[44]), .ALIVE(GRID_OUT[44]),
    .ME_N(CELL_5_4_me_n), .ME_S(CELL_5_4_me_s), .ME_E(CELL_5_4_me_e), .ME_W(CELL_5_4_me_w));
  single_cell CELL_6_4 (
    .NE(CELL_5_5_me_s), .N(CELL_5_4_me_s), .NW(CELL_5_3_me_s), .W(CELL_6_3_me_e), .E(CELL_6_5_me_w),
    .SW(CELL_7_3_me_n), .S(CELL_7_4_me_n), .SE(CELL_7_5_me_n), .ME(GRID_IN[52]), .ALIVE(GRID_OUT[52]),
    .ME_N(CELL_6_4_me_n), .ME_S(CELL_6_4_me_s), .ME_E(CELL_6_4_me_e), .ME_W(CELL_6_4_me_w));
  single_cell CELL_7_4 (
    .NE(CELL_6_5_me_s), .N(CELL_6_4_me_s), .NW(CELL_6_3_me_s), .W(CELL_7_3_me_e), .E(CELL_7_5_me_w),
    .ME(GRID_IN[60]), .ALIVE(GRID_OUT[60]), .ME_N(CELL_7_4_me_n), .ME_E(CELL_7_4_me_e), .ME_W(CELL_7_4_me_w));  // open: SW, S, SE, ME_S
  single_cell CELL_0_5 (
    .W(CELL_0_4_me_e), .E(CELL_0_6_me_w), .SW(CELL_1_4_me_n), .S(CELL_1_5_me_n), .SE(CELL_1_6_me_n),
    .ME(GRID_IN[5]), .ALIVE(GRID_OUT[5]), .ME_S(CELL_0_5_me_s), .ME_E(CELL_0_5_me_e), .ME_W(CELL_0_5_me_w));  // open: NE, N, NW, ME_N
  single_cell CELL_1_5 (
    .NE(CELL_0_6_me_s), .N(CELL_0_5_me_s), .NW(CELL_0_4_me_s), .W(CELL_1_4_me_e), .E(CELL_1_6_me_w),
    .SW(CELL_2_4_me_n), .S(CELL_2_5_me_n), .SE(CELL_2_6_me_n), .ME(GRID_IN[13]), .ALIVE(GRID_OUT[13]),
    .ME_N(CELL_1_5_me_n), .ME_S(CELL_1_5_me_s), .ME_E(CELL_1_5_me_e), .ME_W(CELL_1_5_me_w));
  single_cell CELL_2_5 (
    .NE(CELL_1_6_me_s), .N(CELL_1_5_me_s), .NW(CELL_1_4_me_s), .W(CELL_2_4_me_e), .E(CELL_2_6_me_w),
    .SW(CELL_3_4_me_n), .S(CELL_3_5_me_n), .SE(CELL_3_6_me_n), .ME(GRID_IN[21]), .ALIVE(GRID_OUT[21]),
    .ME_N(CELL_2_5_me_n), .ME_S(CELL_2_5_me_s), .ME_E(CELL_2_5_me_e), .ME_W(CELL_2_5_me_w));
  single_cell CELL_3_5 (
    .NE(CELL_2_6_me_s), .N(CELL_2_5_me_s), .NW(CELL_2_4_me_s), .W(CELL_3_4_me_e), .E(CELL_3_6_me_w),
    .SW(CELL_4_4_me_n), .S(CELL_4_5_me_n), .SE(CELL_4_6_me_n), .ME(GRID_IN[29]), .ALIVE(GRID_OUT[29]),
    .ME_N(CELL_3_5_me_n), .ME_S(CELL_3_5_me_s), .ME_E(CELL_3_5_me_e), .ME_W(CELL_3_5_me_w));
  single_cell CELL_4_5 (
    .NE(CELL_3_6_me_s), .N(CELL_3_5_me_s), .NW(CELL_3_4_me_s), .W(CELL_4_4_me_e), .E(CELL_4_6_me_w),
    .SW(CELL_5_4_me_n), .S(CELL_5_5_me_n), .SE(CELL_5_6_me_n), .ME(GRID_IN[37]), .ALIVE(GRID_OUT[37]),
    .ME_N(CELL_4_5_me_n), .ME_S(CELL_4_5_me_s), .ME_E(CELL_4_5_me_e), .ME_W(CELL_4_5_me_w));
  single_cell CELL_5_5 (
    .NE(CELL_4_6_me_s), .N(CELL_4_5_me_s), .NW(CELL_4_4_me_s), .W(CELL_5_4_me_e), .E(CELL_5_6_me_w),
    .SW(CELL_6_4_me_n), .S(CELL_6_5_me_n), .SE(CELL_6_6_me_n), .ME(GRID_IN[45]), .ALIVE(GRID_OUT[45]),
    .ME_N(CELL_5_5_me_n), .ME_S(CELL_5_5_me_s), .ME_E(CELL_5_5_me_e), .ME_W(CELL_5_5_me_w));
  single_cell CELL_6_5 (
    .NE(CELL_5_6_me_s), .N(CELL_5_5_me_s), .NW(CELL_5_4_me_s), .W(CELL_6_4_me_e), .E(CELL_6_6_me_w),
    .SW(CELL_7_4_me_n), .S(CELL_7_5_me_n), .SE(CELL_7_6_me_n), .ME(GRID_IN[53]), .ALIVE(GRID_OUT[53]),
    .ME_N(CELL_6_5_me_n), .ME_S(CELL_6_5_me_s), .ME_E(CELL_6_5_me_e), .ME_W(CELL_6_5_me_w));
  single_cell CELL_7_5 (
    .NE(CELL_6_6_me_s), .N(CELL_6_5_me_s), .NW(CELL_6_4_me_s), .W(CELL_7_4_me_e), .E(CELL_7_6_me_w),
    .ME(GRID_IN[61]), .ALIVE(GRID_OUT[61]), .ME_N(CELL_7_5_me_n), .ME_E(CELL_7_5_me_e), .ME_W(CELL_7_5_me_w));  // open: SW, S, SE, ME_S
  single_cell CELL_0_6 (
    .W(CELL_0_5_me_e), .E(CELL_0_7_me_w), .SW(CELL_1_5_me_n), .S(CELL_1_6_me_n), .SE(CELL_1_7_me_n),
    .ME(GRID_IN[6]), .ALIVE(GRID_OUT[6]), .ME_S(CELL_0_6_me_s), .ME_E(CELL_0_6_me_e), .ME_W(CELL_0_6_me_w));  // open: NE, N, NW, ME_N
  single_cell CELL_1_6 (
    .NE(CELL_0_7_me_s), .N(CELL_0_6_me_s), .NW(CELL_0_5_me_s), .W(CELL_1_5_me_e), .E(CELL_1_7_me_w),
    .SW(CELL_2_5_me_n), .S(CELL_2_6_me_n), .SE(CELL_2_7_me_n), .ME(GRID_IN[14]), .ALIVE(GRID_OUT[14]),
    .ME_N(CELL_1_6_me_n), .ME_S(CELL_1_6_me_s), .ME_E(CELL_1_6_me_e), .ME_W(CELL_1_6_me_w));
  single_cell CELL_2_6 (
    .NE(CELL_1_7_me_s), .N(CELL_1_6_me_s), .NW(CELL_1_5_me_s), .W(CELL_2_5_me_e), .E(CELL_2_7_me_w),
    .SW(CELL_3_5_me_n), .S(CELL_3_6_me_n), .SE(CELL_3_7_me_n), .ME(GRID_IN[22]), .ALIVE(GRID_OUT[22]),
    .ME_N(CELL_2_6_me_n), .ME_S(CELL_2_6_me_s), .ME_E(CELL_2_6_me_e), .ME_W(CELL_2_6_me_w));
  single_cell CELL_3_6 (
    .NE(CELL_2_7_me_s), .N(CELL_2_6_me_s), .NW(CELL_2_5_me_s), .W(CELL_3_5_me_e), .E(CELL_3_7_me_w),
    .SW(CELL_4_5_me_n), .S(CELL_4_6_me_n), .SE(CELL_4_7_me_n), .ME(GRID_IN[30]), .ALIVE(GRID_OUT[30]),
    .ME_N(CELL_3_6_me_n), .ME_S(CELL_3_6_me_s), .ME_E(CELL_3_6_me_e), .ME_W(CELL_3_6_me_w));
  single_cell CELL_4_6 (
    .NE(CELL_3_7_me_s), .N(CELL_3_6_me_s), .NW(CELL_3_5_me_s), .W(CELL_4_5_me_e), .E(CELL_4_7_me_w),
    .SW(CELL_5_5_me_n), .S(CELL_5_6_me_n), .SE(CELL_5_7_me_n), .ME(GRID_IN[38]), .ALIVE(GRID_OUT[38]),
    .ME_N(CELL_4_6_me_n), .ME_S(CELL_4_6_me_s), .ME_E(CELL_4_6_me_e), .ME_W(CELL_4_6_me_w));
  single_cell CELL_5_6 (
    .NE(CELL_4_7_me_s), .N(CELL_4_6_me_s), .NW(CELL_4_5_me_s), .W(CELL_5_5_me_e), .E(CELL_5_7_me_w),
    .SW(CELL_6_5_me_n), .S(CELL_6_6_me_n), .SE(CELL_6_7_me_n), .ME(GRID_IN[46]), .ALIVE(GRID_OUT[46]),
    .ME_N(CELL_5_6_me_n), .ME_S(CELL_5_6_me_s), .ME_E(CELL_5_6_me_e), .ME_W(CELL_5_6_me_w));
  single_cell CELL_6_6 (
    .NE(CELL_5_7_me_s), .N(CELL_5_6_me_s), .NW(CELL_5_5_me_s), .W(CELL_6_5_me_e), .E(CELL_6_7_me_w),
    .SW(CELL_7_5_me_n), .S(CELL_7_6_me_n), .SE(CELL_7_7_me_n), .ME(GRID_IN[54]), .ALIVE(GRID_OUT[54]),
    .ME_N(CELL_6_6_me_n), .ME_S(CELL_6_6_me_s), .ME_E(CELL_6_6_me_e), .ME_W(CELL_6_6_me_w));
  single_cell CELL_7_6 (
    .NE(CELL_6_7_me_s), .N(CELL_6_6_me_s), .NW(CELL_6_5_me_s), .W(CELL_7_5_me_e), .E(CELL_7_7_me_w),
    .ME(GRID_IN[62]), .ALIVE(GRID_OUT[62]), .ME_N(CELL_7_6_me_n), .ME_E(CELL_7_6_me_e), .ME_W(CELL_7_6_me_w));  // open: SW, S, SE, ME_S
  single_cell CELL_0_7 (
    .W(CELL_0_6_me_e), .SW(CELL_1_6_me_n), .S(CELL_1_7_me_n), .ME(GRID_IN[7]), .ALIVE(GRID_OUT[7]),
    .ME_S(CELL_0_7_me_s), .ME_W(CELL_0_7_me_w));  // open: NE, N, NW, E, SE, ME_N, ME_E
  single_cell CELL_1_7 (
    .N(CELL_0_7_me_s), .NW(CELL_0_6_me_s), .W(CELL_1_6_me_e), .SW(CELL_2_6_me_n), .S(CELL_2_7_me_n),
    .ME(GRID_IN[15]), .ALIVE(GRID_OUT[15]), .ME_N(CELL_1_7_me_n), .ME_S(CELL_1_7_me_s), .ME_W(CELL_1_7_me_w));  // open: NE, E, SE, ME_E
  single_cell CELL_2_7 (
    .N(CELL_1_7_me_s), .NW(CELL_1_6_me_s), .W(CELL_2_6_me_e), .SW(CELL_3_6_me_n), .S(CELL_3_7_me_n),
    .ME(GRID_IN[23]), .ALIVE(GRID_OUT[23]), .ME_N(CELL_2_7_me_n), .ME_S(CELL_2_7_me_s), .ME_W(CELL_2_7_me_w));  // open: NE, E, SE, ME_E
  single_cell CELL_3_7 (
    .N(CELL_2_7_me_s), .NW(CELL_2_6_me_s), .W(CELL_3_6_me_e), .SW(CELL_4_6_me_n), .S(CELL_4_7_me_n),
    .ME(GRID_IN[31]), .ALIVE(GRID_OUT[31]), .ME_N(CELL_3_7_me_n), .ME_S(CELL_3_7_me_s), .ME_W(CELL_3_7_me_w));  // open: NE, E, SE, ME_E
  single_cell CELL_4_7 (
    .N(CELL_3_7_me_s), .NW(CELL_3_6_me_s), .W(CELL_4_6_me_e), .SW(CELL_5_6_me_n), .S(CELL_5_7_me_n),
    .ME(GRID_IN[39]), .ALIVE(GRID_OUT[39]), .ME_N(CELL_4_7_me_n), .ME_S(CELL_4_7_me_s), .ME_W(CELL_4_7_me_w));  // open: NE, E, SE, ME_E
  single_cell CELL_5_7 (
    .N(CELL_4_7_me_s), .NW(CELL_4_6_me_s), .W(CELL_5_6_me_e), .SW(CELL_6_6_me_n), .S(CELL_6_7_me_n),
    .ME(GRID_IN[47]), .ALIVE(GRID_OUT[47]), .ME_N(CELL_5_7_me_n), .ME_S(CELL_5_7_me_s), .ME_W(CELL_5_7_me_w));  // open: NE, E, SE, ME_E
  single_cell CELL_6_7 (
    .N(CELL_5_7_me_s), .NW(CELL_5_6_me_s), .W(CELL_6_6_me_e), .SW(CELL_7_6_me_n), .S(CELL_7_7_me_n),
    .ME(GRID_IN[55]), .ALIVE(GRID_OUT[55]), .ME_N(CELL_6_7_me_n), .ME_S(CELL_6_7_me_s), .ME_W(CELL_6_7_me_w));  // open: NE, E, SE, ME_E
  single_cell CELL_7_7 (
    .N(CELL_6_7_me_s), .NW(CELL_6_6_me_s), .W(CELL_7_6_me_e), .ME(GRID_IN[63]), .ALIVE(GRID_OUT[63]),
    .ME_N(CELL_7_7_me_n), .ME_W(CELL_7_7_me_w));  // open: NE, E, SW, S, SE, ME_S, ME_E
endmodule

module main_shift_based (
  input  DATA_IN,
  input  [1:0] MODE,
  input  RESET,
  output DATA_OUT
);

  wire and_1_out, CLK_out, decoder_1_out0, decoder_1_out1, decoder_1_out2, decoder_1_out3, not_1_out,
       or_1_out;
  wire [7:0] cell_grid_1_grid_out, cell_grid_1_grid_out_2, cell_grid_1_grid_out_3, cell_grid_1_grid_out_4,
       cell_grid_1_grid_out_5, cell_grid_1_grid_out_6, cell_grid_1_grid_out_7, cell_grid_1_grid_out_8;
  wire [63:0] data_input_handler_serial_1_data, data_output_handler_1_paralel_out, system_memory_1_mem_out;

  Decoder #(.select(2)) decoder_1 (
    .out0(decoder_1_out0), .out1(decoder_1_out1), .out2(decoder_1_out2), .out3(decoder_1_out3), .sel(MODE));  // open: en
  Clock CLK (.out(CLK_out));
  not not_1 (not_1_out, decoder_1_out0);
  and and_1 (and_1_out, not_1_out, CLK_out);
  or or_1 (or_1_out, decoder_1_out2, decoder_1_out1);
  data_input_handler_serial data_input_handler_serial_1 (
    .RST(RESET), .EN(decoder_1_out1), .CLK(and_1_out), .DATA_IN(DATA_IN),
    .DATA(data_input_handler_serial_1_data));
  DotMatrix #(.inputtype("row"), .matrixcols(8), .matrixrows(8)) dotmatrix_1 (
    .row0(data_input_handler_serial_1_data[7:0]), .row1(data_input_handler_serial_1_data[15:8]),
    .row2(data_input_handler_serial_1_data[23:16]), .row3(data_input_handler_serial_1_data[31:24]),
    .row4(data_input_handler_serial_1_data[39:32]), .row5(data_input_handler_serial_1_data[47:40]),
    .row6(data_input_handler_serial_1_data[55:48]), .row7(data_input_handler_serial_1_data[63:56]));
  system_memory system_memory_1 (
    .GRID_IN({cell_grid_1_grid_out_8, cell_grid_1_grid_out_7, cell_grid_1_grid_out_6, cell_grid_1_grid_out_5, cell_grid_1_grid_out_4, cell_grid_1_grid_out_3, cell_grid_1_grid_out_2, cell_grid_1_grid_out}),
    .INITIAL_IN(data_input_handler_serial_1_data), .WRITE_ENABLE(or_1_out), .LOAD_RUN(decoder_1_out2),
    .CLK(and_1_out), .RESET(RESET), .MEM_OUT(system_memory_1_mem_out));
  // Probe on system_memory_1_mem_out
  DotMatrix #(.inputtype("row"), .matrixcols(8), .matrixrows(8)) CURRENT_STAGE (
    .row0(system_memory_1_mem_out[7:0]), .row1(system_memory_1_mem_out[15:8]),
    .row2(system_memory_1_mem_out[23:16]), .row3(system_memory_1_mem_out[31:24]),
    .row4(system_memory_1_mem_out[39:32]), .row5(system_memory_1_mem_out[47:40]),
    .row6(system_memory_1_mem_out[55:48]), .row7(system_memory_1_mem_out[63:56]));
  cell_grid cell_grid_1 (
    .GRID_IN(system_memory_1_mem_out),
    .GRID_OUT({cell_grid_1_grid_out_8, cell_grid_1_grid_out_7, cell_grid_1_grid_out_6, cell_grid_1_grid_out_5, cell_grid_1_grid_out_4, cell_grid_1_grid_out_3, cell_grid_1_grid_out_2, cell_grid_1_grid_out}));
  // Probe on {cell_grid_1_grid_out_8, cell_grid_1_grid_out_7, cell_grid_1_grid_out_6, cell_grid_1_grid_out_5, cell_grid_1_grid_out_4, cell_grid_1_grid_out_3, cell_grid_1_grid_out_2, cell_grid_1_grid_out}
  DotMatrix #(.inputtype("row"), .matrixcols(8), .matrixrows(8)) NEXT_STAGE (
    .row0(cell_grid_1_grid_out), .row1(cell_grid_1_grid_out_2), .row2(cell_grid_1_grid_out_3),
    .row3(cell_grid_1_grid_out_4), .row4(cell_grid_1_grid_out_5), .row5(cell_grid_1_grid_out_6),
    .row6(cell_grid_1_grid_out_7), .row7(cell_grid_1_grid_out_8));
  data_output_handler data_output_handler_1 (
    .RST(RESET), .LOAD_MODE(or_1_out), .OUTPUT_MODE(decoder_1_out3), .CLK(and_1_out),
    .DATA({cell_grid_1_grid_out_8, cell_grid_1_grid_out_7, cell_grid_1_grid_out_6, cell_grid_1_grid_out_5, cell_grid_1_grid_out_4, cell_grid_1_grid_out_3, cell_grid_1_grid_out_2, cell_grid_1_grid_out}),
    .DATA_OUT(DATA_OUT), .PARALEL_OUT(data_output_handler_1_paralel_out));
  DotMatrix #(.inputtype("row"), .matrixcols(8), .matrixrows(8)) dotmatrix_2 (
    .row0(data_output_handler_1_paralel_out[7:0]), .row1(data_output_handler_1_paralel_out[15:8]),
    .row2(data_output_handler_1_paralel_out[23:16]), .row3(data_output_handler_1_paralel_out[31:24]),
    .row4(data_output_handler_1_paralel_out[39:32]), .row5(data_output_handler_1_paralel_out[47:40]),
    .row6(data_output_handler_1_paralel_out[55:48]), .row7(data_output_handler_1_paralel_out[63:56]));

  // Notes on the sheet:
  //   1. Set "MODE" to "01" (i.e. data in) and run clock 64 times to shift in all data
  //   2. Set mode to "10" (i.e. run) and clock to run the system
  //   3. To read out, set mode to "11" (i.e. data out), then clock 64 times to read out data
  //   4. Set RESET to high to async reset everything
  //   5. Set mode to "11" to disable clocking
  //   These are only accurate when in run mode
  //   This is not accurate once we start clocking data out
endmodule

module data_input_handler_serial_stop_64 (
  input  DATA_IN,
  input  EN,
  input  CLK,
  input  RST,
  output [63:0] DATA,
  output DONE,
  output [5:0] COUNT_OUT
);

  wire and_1_out, counter_1_carry, not_1_out;

  Counter #(.max('h3f), .ongoal("stay"), .width(6)) counter_1 (
    .clr(RST), .count(EN), .clk(CLK), .carry(counter_1_carry), .Q(COUNT_OUT));  // open: load, up, D
  D_Flip_Flop d_ff_1 (.D(counter_1_carry), .clk(CLK), .Q(DONE), .reset(RST));  // open: Qn, preset
  and and_1 (and_1_out, EN, not_1_out);
  not not_1 (not_1_out, DONE);
  // Shift_Register #(.length(64)) shift_register_1: pin names not known; wires that end beside it: RST, and_1_out, CLK, DATA_IN, DATA[63], DATA[62], DATA[61], DATA[60], DATA[59], DATA[58], DATA[57], DATA[56], DATA[55], DATA[54], DATA[53], DATA[52]
  // Probe on DATA

  // Notes on the sheet:
  //   DFF delays toggle by 1 cycle, which we need to shift in last value
  //   1. Set the input data to read in serially
  //   2. Toggle reset to restart system
  //   3. Enable EN and clock
  //   4. When all 64 read, system will stop and DONE will be high
endmodule

module data_input_handler_serial (
  input  RST,
  input  EN,
  input  CLK,
  input  DATA_IN,
  output [63:0] DATA
);

  // Shift_Register #(.length(64)) shift_register_1: pin names not known; wires that end beside it: RST, EN, CLK, DATA_IN, DATA[63], DATA[62], DATA[61], DATA[60], DATA[59], DATA[58], DATA[57], DATA[56], DATA[55], DATA[54], DATA[53], DATA[52]
  // Probe on DATA

  // Notes on the sheet:
  //   1. Toggle reset to restart system
  //   2. Enable EN and clock to shift data in
endmodule

module system_memory (
  input  [63:0] GRID_IN,
  input  [63:0] INITIAL_IN,
  input  WRITE_ENABLE,
  input  LOAD_RUN,
  input  CLK,
  input  RESET,
  output [63:0] MEM_OUT
);

  wire [63:0] multiplexer_1_out;

  Multiplexer #(.width(64)) multiplexer_1 (.in0(INITIAL_IN), .in1(GRID_IN), .out(multiplexer_1_out), .sel(LOAD_RUN));
  Register #(.width(64)) register_1 (.D(multiplexer_1_out), .en(WRITE_ENABLE), .clk(CLK), .Q(MEM_OUT), .clr(RESET));

  // Notes on the sheet:
  //   Loads in and stores memory in register. When in load mode, data to load is passed through to help with debugging
endmodule

module data_output_handler (
  input  RST,
  input  LOAD_MODE,
  input  OUTPUT_MODE,
  input  CLK,
  input  [63:0] DATA,
  output [63:0] PARALEL_OUT,
  output DATA_OUT
);

  // Shift_Register #(.length(64)) shift_register_1: pin names not known; wires that end beside it: RST, LOAD_MODE, OUTPUT_MODE, CLK, 1'b0, DATA[0], DATA[1], DATA[2], DATA[3], DATA[4], DATA[5], DATA[6], DATA[7], DATA[8], DATA[9], DATA[10], DATA[11], PARALEL_OUT[0], PARALEL_OUT[1], PARALEL_OUT[2], PARALEL_OUT[3], PARALEL_OUT[4], PARALEL_OUT[5], PARALEL_OUT[6], PARALEL_OUT[7], PARALEL_OUT[8], PARALEL_OUT[9], PARALEL_OUT[10], PARALEL_OUT[11]

  assign PARALEL_OUT[63] = DATA_OUT;

  // Notes on the sheet:
  //   Const 0 ensures we shift in zeros
endmodule

module serial_input_and_memory (
  input  RST,
  input  RUN_MODE,
  input  LOAD_MODE,
  input  CLK,
  input  DATA_IN,
  input  [63:0] GRID_IN,
  output [63:0] DATA
);

  // Shift_Register #(.length(64)) shift_register_1: pin names not known; wires that end beside it: RST, RUN_MODE, LOAD_MODE, CLK, DATA_IN, GRID_IN[63], GRID_IN[62], GRID_IN[61], GRID_IN[60], GRID_IN[59], GRID_IN[58], GRID_IN[57], GRID_IN[56], GRID_IN[55], GRID_IN[54], GRID_IN[53], GRID_IN[52], DATA[63], DATA[62], DATA[61], DATA[60], DATA[59], DATA[58], DATA[57], DATA[56], DATA[55], DATA[54], DATA[53], DATA[52]
  // Probe on DATA

  // Notes on the sheet:
  //   1. Toggle reset to restart system
  //   2. Enable EN and clock to shift data in
  //   Since the shift register has parallel load support, we can use it as the memory instead of a separate set of registers
endmodule

module main_shift_based_v2 (
  input  DATA_IN,
  input  [1:0] MODE,
  input  RESET,
  output DATA_OUT
);

  wire and_1_out, CLK_out, decoder_1_out0, decoder_1_out1, decoder_1_out2, decoder_1_out3, not_1_out,
       or_1_out;
  wire [7:0] cell_grid_1_grid_out, cell_grid_1_grid_out_2, cell_grid_1_grid_out_3, cell_grid_1_grid_out_4,
       cell_grid_1_grid_out_5, cell_grid_1_grid_out_6, cell_grid_1_grid_out_7, cell_grid_1_grid_out_8;
  wire [63:0] data_output_handler_1_paralel_out, serial_input_and_memory_1_data;

  Decoder #(.select(2)) decoder_1 (
    .out0(decoder_1_out0), .out1(decoder_1_out1), .out2(decoder_1_out2), .out3(decoder_1_out3), .sel(MODE));  // open: en
  Clock CLK (.out(CLK_out));
  not not_1 (not_1_out, decoder_1_out0);
  and and_1 (and_1_out, not_1_out, CLK_out);
  or or_1 (or_1_out, decoder_1_out2, decoder_1_out1);
  // Probe on serial_input_and_memory_1_data
  serial_input_and_memory serial_input_and_memory_1 (
    .GRID_IN({cell_grid_1_grid_out_8, cell_grid_1_grid_out_7, cell_grid_1_grid_out_6, cell_grid_1_grid_out_5, cell_grid_1_grid_out_4, cell_grid_1_grid_out_3, cell_grid_1_grid_out_2, cell_grid_1_grid_out}),
    .RST(RESET), .RUN_MODE(decoder_1_out2), .LOAD_MODE(decoder_1_out1), .CLK(and_1_out), .DATA_IN(DATA_IN),
    .DATA(serial_input_and_memory_1_data));
  DotMatrix #(.inputtype("row"), .matrixcols(8), .matrixrows(8)) CURRENT_STAGE (
    .row0(serial_input_and_memory_1_data[7:0]), .row1(serial_input_and_memory_1_data[15:8]),
    .row2(serial_input_and_memory_1_data[23:16]), .row3(serial_input_and_memory_1_data[31:24]),
    .row4(serial_input_and_memory_1_data[39:32]), .row5(serial_input_and_memory_1_data[47:40]),
    .row6(serial_input_and_memory_1_data[55:48]), .row7(serial_input_and_memory_1_data[63:56]));
  cell_grid cell_grid_1 (
    .GRID_IN(serial_input_and_memory_1_data),
    .GRID_OUT({cell_grid_1_grid_out_8, cell_grid_1_grid_out_7, cell_grid_1_grid_out_6, cell_grid_1_grid_out_5, cell_grid_1_grid_out_4, cell_grid_1_grid_out_3, cell_grid_1_grid_out_2, cell_grid_1_grid_out}));
  // Probe on {cell_grid_1_grid_out_8, cell_grid_1_grid_out_7, cell_grid_1_grid_out_6, cell_grid_1_grid_out_5, cell_grid_1_grid_out_4, cell_grid_1_grid_out_3, cell_grid_1_grid_out_2, cell_grid_1_grid_out}
  DotMatrix #(.inputtype("row"), .matrixcols(8), .matrixrows(8)) NEXT_STAGE (
    .row0(cell_grid_1_grid_out), .row1(cell_grid_1_grid_out_2), .row2(cell_grid_1_grid_out_3),
    .row3(cell_grid_1_grid_out_4), .row4(cell_grid_1_grid_out_5), .row5(cell_grid_1_grid_out_6),
    .row6(cell_grid_1_grid_out_7), .row7(cell_grid_1_grid_out_8));
  // Probe on data_output_handler_1_paralel_out
  DotMatrix #(.inputtype("row"), .matrixcols(8), .matrixrows(8)) dotmatrix_1 (
    .row0(data_output_handler_1_paralel_out[7:0]), .row1(data_output_handler_1_paralel_out[15:8]),
    .row2(data_output_handler_1_paralel_out[23:16]), .row3(data_output_handler_1_paralel_out[31:24]),
    .row4(data_output_handler_1_paralel_out[39:32]), .row5(data_output_handler_1_paralel_out[47:40]),
    .row6(data_output_handler_1_paralel_out[55:48]), .row7(data_output_handler_1_paralel_out[63:56]));
  data_output_handler data_output_handler_1 (
    .RST(RESET), .LOAD_MODE(or_1_out), .OUTPUT_MODE(decoder_1_out3), .CLK(and_1_out),
    .DATA({cell_grid_1_grid_out_8, cell_grid_1_grid_out_7, cell_grid_1_grid_out_6, cell_grid_1_grid_out_5, cell_grid_1_grid_out_4, cell_grid_1_grid_out_3, cell_grid_1_grid_out_2, cell_grid_1_grid_out}),
    .DATA_OUT(DATA_OUT), .PARALEL_OUT(data_output_handler_1_paralel_out));

  // Notes on the sheet:
  //   1. Set "MODE" to "01" (i.e. data in) and run clock 64 times to shift in all data
  //   2. Set mode to "10" (i.e. run) and clock to run the system
  //   3. To read out, set mode to "11" (i.e. data out), then clock 64 times to read out data
  //   4. Set RESET to high to async reset everything
  //   5. Set mode to "00" to disable clocking
  //   These are only accurate when in run mode
  //   This needs to stay separate, or shifting out would mess up the stored data
  //   Which would require us to clock back in after each clock out
  //   FIXME: How do I shift out backwards like how VHDL implementation does
  //   This is not accurate once we start clocking data out
endmodule

module fully_combined_memory (
  input  RST,
  input  RUN_MODE,
  input  LOAD_MODE,
  input  CLK,
  input  DATA_IN,
  input  [63:0] GRID_IN,
  input  OUTPUT_MODE,
  output [63:0] DATA,
  output [63:0] PARALEL_OUT,
  output SERIAL_OUT
);

  wire or_1_out;

  // Shift_Register #(.length(64)) shift_register_1: pin names not known; wires that end beside it: RST, RUN_MODE, LOAD_MODE, CLK, DATA_IN, GRID_IN[63], GRID_IN[62], GRID_IN[61], GRID_IN[60], GRID_IN[59], GRID_IN[58], GRID_IN[57], GRID_IN[56], GRID_IN[55], GRID_IN[54], GRID_IN[53], GRID_IN[52], DATA[63], DATA[62], DATA[61], DATA[60], DATA[59], DATA[58], DATA[57], DATA[56], DATA[55], DATA[54], DATA[53], DATA[52]
  // Probe on DATA
  or or_1 (or_1_out, LOAD_MODE, OUTPUT_MODE);
  // Shift_Register #(.length(64)) shift_register_2: pin names not known; wires that end beside it: RST, RUN_MODE, or_1_out, CLK, DATA_IN, GRID_IN[63], GRID_IN[62], GRID_IN[61], GRID_IN[60], GRID_IN[59], GRID_IN[58], GRID_IN[57], GRID_IN[56], GRID_IN[55], GRID_IN[54], GRID_IN[53], GRID_IN[52], PARALEL_OUT[63], PARALEL_OUT[62], PARALEL_OUT[61], PARALEL_OUT[60], PARALEL_OUT[59], PARALEL_OUT[58], PARALEL_OUT[57], PARALEL_OUT[56], PARALEL_OUT[55], PARALEL_OUT[54], PARALEL_OUT[53], PARALEL_OUT[52]

  assign SERIAL_OUT = PARALEL_OUT[0];

  // Notes on the sheet:
  //   1. Toggle reset to restart system
  //   2. Enable EN and clock to shift data in
  //   Since the shift register has parallel load support, we can use it as the memory instead of a separate set of registers
  //   We need 2 shift registers so that shifting out does not wipe internal data
endmodule

module main_shift_based_v3 (
  input  DATA_IN,
  input  [1:0] MODE,
  input  RESET,
  output DATA_OUT
);

  wire and_1_out, CLK_out, decoder_1_out0, decoder_1_out1, decoder_1_out2, decoder_1_out3, not_1_out;
  wire [7:0] cell_grid_1_grid_out, cell_grid_1_grid_out_2, cell_grid_1_grid_out_3, cell_grid_1_grid_out_4,
       cell_grid_1_grid_out_5, cell_grid_1_grid_out_6, cell_grid_1_grid_out_7, cell_grid_1_grid_out_8;
  wire [63:0] fully_combined_memory_1_data, fully_combined_memory_1_paralel_out;

  Decoder #(.select(2)) decoder_1 (
    .out0(decoder_1_out0), .out1(decoder_1_out1), .out2(decoder_1_out2), .out3(decoder_1_out3), .sel(MODE));  // open: en
  Clock CLK (.out(CLK_out));
  not not_1 (not_1_out, decoder_1_out0);
  and and_1 (and_1_out, not_1_out, CLK_out);
  // Probe on fully_combined_memory_1_data
  fully_combined_memory fully_combined_memory_1 (
    .OUTPUT_MODE(decoder_1_out3),
    .GRID_IN({cell_grid_1_grid_out_8, cell_grid_1_grid_out_7, cell_grid_1_grid_out_6, cell_grid_1_grid_out_5, cell_grid_1_grid_out_4, cell_grid_1_grid_out_3, cell_grid_1_grid_out_2, cell_grid_1_grid_out}),
    .RST(RESET), .RUN_MODE(decoder_1_out2), .LOAD_MODE(decoder_1_out1), .CLK(and_1_out), .DATA_IN(DATA_IN),
    .DATA(fully_combined_memory_1_data), .SERIAL_OUT(DATA_OUT),
    .PARALEL_OUT(fully_combined_memory_1_paralel_out));
  DotMatrix #(.inputtype("row"), .matrixcols(8), .matrixrows(8)) CURRENT_STAGE (
    .row0(fully_combined_memory_1_data[7:0]), .row1(fully_combined_memory_1_data[15:8]),
    .row2(fully_combined_memory_1_data[23:16]), .row3(fully_combined_memory_1_data[31:24]),
    .row4(fully_combined_memory_1_data[39:32]), .row5(fully_combined_memory_1_data[47:40]),
    .row6(fully_combined_memory_1_data[55:48]), .row7(fully_combined_memory_1_data[63:56]));
  cell_grid cell_grid_1 (
    .GRID_IN(fully_combined_memory_1_data),
    .GRID_OUT({cell_grid_1_grid_out_8, cell_grid_1_grid_out_7, cell_grid_1_grid_out_6, cell_grid_1_grid_out_5, cell_grid_1_grid_out_4, cell_grid_1_grid_out_3, cell_grid_1_grid_out_2, cell_grid_1_grid_out}));
  // Probe on {cell_grid_1_grid_out_8, cell_grid_1_grid_out_7, cell_grid_1_grid_out_6, cell_grid_1_grid_out_5, cell_grid_1_grid_out_4, cell_grid_1_grid_out_3, cell_grid_1_grid_out_2, cell_grid_1_grid_out}
  DotMatrix #(.inputtype("row"), .matrixcols(8), .matrixrows(8)) NEXT_STAGE (
    .row0(cell_grid_1_grid_out), .row1(cell_grid_1_grid_out_2), .row2(cell_grid_1_grid_out_3),
    .row3(cell_grid_1_grid_out_4), .row4(cell_grid_1_grid_out_5), .row5(cell_grid_1_grid_out_6),
    .row6(cell_grid_1_grid_out_7), .row7(cell_grid_1_grid_out_8));
  // Probe on fully_combined_memory_1_paralel_out
  DotMatrix #(.inputtype("row"), .matrixcols(8), .matrixrows(8)) dotmatrix_1 (
    .row0(fully_combined_memory_1_paralel_out[7:0]), .row1(fully_combined_memory_1_paralel_out[15:8]),
    .row2(fully_combined_memory_1_paralel_out[23:16]), .row3(fully_combined_memory_1_paralel_out[31:24]),
    .row4(fully_combined_memory_1_paralel_out[39:32]), .row5(fully_combined_memory_1_paralel_out[47:40]),
    .row6(fully_combined_memory_1_paralel_out[55:48]), .row7(fully_combined_memory_1_paralel_out[63:56]));

  // Notes on the sheet:
  //   1. Set "MODE" to "01" (i.e. data in) and run clock 64 times to shift in all data
  //   2. Set mode to "10" (i.e. run) and clock to run the system
  //   3. To read out, set mode to "11" (i.e. data out), then clock 64 times to read out data
  //   4. Set RESET to high to async reset everything
  //   5. Set mode to "00" to disable clocking
  //   These are only accurate when in run mode
  //   This needs to stay separate, or shifting out would mess up the stored data
  //   Which would require us to clock back in after each clock out
  //   FIXME: How do I shift out backwards like how VHDL implementation does
  //   This is not accurate once we start clocking data out
endmodule

module neighbor_check (
  input  ME,
  input  NE,
  input  N,
  input  NW,
  input  W,
  input  E,
  input  SW,
  input  S,
  input  SE
);

  // NAND_Gate nand_1 has open pins: in0=NE, in1=N, out=open
endmodule

module looparound_memory (
  input  LOAD_MODE,
  input  OUTPUT_MODE,
  input  RST,
  input  RUN_MODE,
  input  DATA_IN,
  input  CLK,
  input  [63:0] GRID_IN,
  output [63:0] DATA,
  output SERIAL_OUT
);

  wire multiplexer_1_out, or_1_out;

  Multiplexer multiplexer_1 (.in0(DATA_IN), .in1(DATA[0]), .out(multiplexer_1_out), .sel(OUTPUT_MODE));
  or or_1 (or_1_out, LOAD_MODE, OUTPUT_MODE);
  // Shift_Register #(.length(64)) shift_register_1: pin names not known; wires that end beside it: RST, RUN_MODE, or_1_out, CLK, multiplexer_1_out, GRID_IN[63], GRID_IN[62], GRID_IN[61], GRID_IN[60], GRID_IN[59], GRID_IN[58], GRID_IN[57], GRID_IN[56], GRID_IN[55], GRID_IN[54], GRID_IN[53], GRID_IN[52], DATA[63], DATA[62], DATA[61], DATA[60], DATA[59], DATA[58], DATA[57], DATA[56], DATA[55], DATA[54], DATA[53], DATA[52]
  // Probe on DATA

  assign SERIAL_OUT = DATA[0];

  // Notes on the sheet:
  //   Like "fully_combined_memory" but instead of using two shift registers, 
  //   we only use 1, but when shifting out, we also loop the data around back into
  //   the system.
  //   Downside is that it means we can't do partial reads. You must always read exactly the size of the system
endmodule

module main_shift_based_v4 (
  input  DATA_IN,
  input  [1:0] MODE,
  input  RESET,
  output DATA_OUT
);

  wire and_1_out, CLK_out, decoder_1_out0, decoder_1_out1, decoder_1_out2, decoder_1_out3, not_1_out;
  wire [7:0] cell_grid_1_grid_out, cell_grid_1_grid_out_2, cell_grid_1_grid_out_3, cell_grid_1_grid_out_4,
       cell_grid_1_grid_out_5, cell_grid_1_grid_out_6, cell_grid_1_grid_out_7, cell_grid_1_grid_out_8;
  wire [63:0] looparound_memory_1_data;

  Decoder #(.select(2)) decoder_1 (
    .out0(decoder_1_out0), .out1(decoder_1_out1), .out2(decoder_1_out2), .out3(decoder_1_out3), .sel(MODE));  // open: en
  Clock CLK (.out(CLK_out));
  not not_1 (not_1_out, decoder_1_out0);
  and and_1 (and_1_out, not_1_out, CLK_out);
  // Probe on looparound_memory_1_data
  looparound_memory looparound_memory_1 (
    .DATA_IN(DATA_IN), .OUTPUT_MODE(decoder_1_out3), .LOAD_MODE(decoder_1_out1),
    .GRID_IN({cell_grid_1_grid_out_8, cell_grid_1_grid_out_7, cell_grid_1_grid_out_6, cell_grid_1_grid_out_5, cell_grid_1_grid_out_4, cell_grid_1_grid_out_3, cell_grid_1_grid_out_2, cell_grid_1_grid_out}),
    .RST(RESET), .RUN_MODE(decoder_1_out2), .CLK(and_1_out), .SERIAL_OUT(DATA_OUT),
    .DATA(looparound_memory_1_data));
  DotMatrix #(.inputtype("row"), .matrixcols(8), .matrixrows(8)) CURRENT_STAGE (
    .row0(looparound_memory_1_data[7:0]), .row1(looparound_memory_1_data[15:8]),
    .row2(looparound_memory_1_data[23:16]), .row3(looparound_memory_1_data[31:24]),
    .row4(looparound_memory_1_data[39:32]), .row5(looparound_memory_1_data[47:40]),
    .row6(looparound_memory_1_data[55:48]), .row7(looparound_memory_1_data[63:56]));
  // Probe on {cell_grid_1_grid_out_8, cell_grid_1_grid_out_7, cell_grid_1_grid_out_6, cell_grid_1_grid_out_5, cell_grid_1_grid_out_4, cell_grid_1_grid_out_3, cell_grid_1_grid_out_2, cell_grid_1_grid_out}
  DotMatrix #(.inputtype("row"), .matrixcols(8), .matrixrows(8)) NEXT_STAGE (
    .row0(cell_grid_1_grid_out), .row1(cell_grid_1_grid_out_2), .row2(cell_grid_1_grid_out_3),
    .row3(cell_grid_1_grid_out_4), .row4(cell_grid_1_grid_out_5), .row5(cell_grid_1_grid_out_6),
    .row6(cell_grid_1_grid_out_7), .row7(cell_grid_1_grid_out_8));
  cell_grid cell_grid_1 (
    .GRID_IN(looparound_memory_1_data),
    .GRID_OUT({cell_grid_1_grid_out_8, cell_grid_1_grid_out_7, cell_grid_1_grid_out_6, cell_grid_1_grid_out_5, cell_grid_1_grid_out_4, cell_grid_1_grid_out_3, cell_grid_1_grid_out_2, cell_grid_1_grid_out}));

  // Notes on the sheet:
  //   1. Set "MODE" to "01" (i.e. data in) and run clock 64 times to shift in all data
  //   2. Set mode to "10" (i.e. run) and clock to run the system
  //   3. To read out, set mode to "11" (i.e. data out), then clock 64 times to read out data
  //   4. Set RESET to high to async reset everything
  //   5. Set mode to "00" to disable clocking
  //   These are only accurate when in run mode
  //   Which would require us to clock back in after each clock out
  //   This needs to stay separate, or shifting out would mess up the stored data
  //   FIXME: How do I shift out backwards like how VHDL implementation does
endmodule
